# Fritzing sketch Mikrobus_InfraRed_LIRC (saved by Fritzing 0.9.2b)
breadboards: 1

parts:
  Part1 = Mikrobus - Cobbler
  IR1 = TSOP312.., 314.. [package=THT]
  Q2 = NPN-Transistor [package="TO92 [THT]"]
  LED3 = smd LED [color="Red (633nm)" package="0603 [SMD]"]
  LED4 = smd LED [color="Red (633nm)" package="0603 [SMD]"]
  R2 = Resistor [tolerance=±5% resistance=10k package="1206 [SMD]"]

nets:
  N1: Part1.+3.3V, IR1.Vs
  GND: Part1.GND, Q2.E, R2.Pin_0
  N2: Part1.+5V, LED3.anode
  N3: Q2.B, R2.Pin_1
  N4: LED3.cathode, LED4.anode

notes:
  Need to check pin outs of receiver as Fritzing does not match web page
  http://alexba.in/blog/2013/03/09/raspberrypi-ir-schematic-for-lirc/
  Web uses GPIO22 & 23
  For Mikrobus use GPIO18 PWM & GPIO6 INT

custom parts:
  Mikrobus - Cobbler: The idea of the Mikrobus cobbler is to plug it into a breadboard and connect the 40 way connector to the 40 way connector on the Raspberry Pi B+, 2B using a Ribbon cable. You can then prototype your Mikrobus board and test with the Raspberry Pi
